# Fritzing sketch esphome--water-level-meter (saved by Fritzing 0.9.6b)

parts:
  A1 = Esp32-c3 super mini
  M1 = JSN-SRO4T [package=THT]
  LLC2 = Logic Level Converter [part_number="5V-3.3V Level Shifter" package="Breakout board"]
  Part1 = SO-24x [chip_label=SO-24x package=SO(x)]  # not connected
  U1 = IC, DIP package, 6 pins [chip_label=AQV258 part_number="AQV258 PhotoMOS"]
  HLK-PM1 = HLK-PM01
  R1 = Resistor [tolerance=±5% power=0.25 resistance=470 package=THT]

nets:
  N1: A1.Pin_5, U1.pin1, R1.Pin_1
  N2: A1.Pin_6, R1.Pin_0
  N3: A1.Pin_7, LLC2.LV3
  N4: A1.Pin_8, LLC2.LV4
  N5: A1.Pin_14, A1.Pin_15, M1.pin1, LLC2.LV, LLC2.L-GND, LLC2.H-GND, HLK-PM1.-Vo
  N6: A1.Pin_16, LLC2.HV, U1.pin5, HLK-PM1.+Vo
  N7: M1.pin2, LLC2.HV3
  N8: M1.pin3, LLC2.HV4
  N9: M1.pin4, U1.pin4

custom parts:
  Esp32-c3 super mini: ESP32-C3 Development Board ESP32 SuperMini Development Board ESP32 Development Board WiFi Bluetooth.
  JSN-SRO4T: JSN-SR04T Waterproof Ultrasonic Distance Measuring Module Integrated Ultrasonic Detection Module DC 5V.
  Logic Level Converter: 5V to/from 3.3V logic level converter
